# Fritzing sketch fritzing (saved by Fritzing 0.9.4)
breadboards: 1

parts:
  Parça1 = Arduino Uno (Rev3)
  LCM1602_IIC1 = LCM1602 IIC [part_number="LCM1602 IIC" chip_label="LCM1602 IIC" package="DIP (Dual Inline) [THT]"]
  LCD1 = LCD screen
  LED1 = LED - 5mm [color="Red (633nm)" package="5 mm [THT]"]
  LED2 = LED - 5mm [color="Green (570nm)" package="5 mm [THT]"]
  R1 = Resistor [tolerance=±5% resistance=220 package=THT]
  R2 = Resistor [tolerance=±5% resistance=220 package=THT]
  J1 = Piezo Speaker
  S1 = Pushbutton [package="[THT]"]
  R3 = Resistor [tolerance=±5% resistance=10k package=THT]
  DHT1 = DHT11 Humitidy and Temperature Sensor
  J2 = Basic Servo
  RE1 = Rotary Encoder [package=THT]
  Parça2 = RFID-RC522-v3

nets:
  N1: Parça1.A0, RE1.EncoderPinC
  N2: Parça1.A2, LCM1602_IIC1.SDA
  N3: Parça1.A5/SCL, LCM1602_IIC1.SCL
  N4: Parça1.D9_PWM, S1.Pin_1, S1.Pin_2, R3.Pin_0
  N5: Parça1.D10_PWM/SS, Parça2.RST
  N6: Parça1.D11_PWM/MOSI, Parça2.SCK
  N7: Parça1.D12/MISO, Parça2.MOSI
  N8: Parça1.D13/SCK, Parça2.MISO
  N9: Parça1.D1/TX, DHT1.DATA
  N10: Parça1.D2, J1.pin2
  N11: Parça1.D3_PWM, R1.Pin_0
  N12: Parça1.D4, R2.Pin_0
  N13: Parça1.D5_PWM, Parça2.SDA
  N14: Parça1.D6_PWM, J2.pulse
  3V3: Parça1.3V3, S1.Pin_3, S1.Pin_4, RE1.EncoderPinA, Parça2.3.3V
  VCC: Parça1.5V, LCM1602_IIC1.VCC, DHT1.VDD, J2.vcc
  GND: Parça1.GND, LCM1602_IIC1.GND, J1.pin1, R3.Pin_1, DHT1.GND, J2.gnd, RE1.EncoderPinB, Parça2.GND
  VSS: LCM1602_IIC1.VSS, LCD1.VSS
  VDD: LCM1602_IIC1.VDD, LCD1.VDD
  N15: LCM1602_IIC1.V0, LCD1.V0
  N16: LCM1602_IIC1.RS, LCD1.RS
  N17: LCM1602_IIC1.RW, LCD1.R/W
  N18: LCM1602_IIC1.E, LCD1.E
  N19: LCM1602_IIC1.D0, LCD1.DB0
  N20: LCM1602_IIC1.D1, LCD1.DB1
  N21: LCM1602_IIC1.D2, LCD1.DB2
  N22: LCM1602_IIC1.D3, LCD1.DB3
  N23: LCM1602_IIC1.D4, LCD1.DB4
  N24: LCM1602_IIC1.D5, LCD1.DB5
  N25: LCM1602_IIC1.D6, LCD1.DB6
  N26: LCM1602_IIC1.D7, LCD1.DB7
  N27: LCM1602_IIC1.A, LCD1.LED+
  N28: LCM1602_IIC1.K, LCD1.LED-
  N29: LED1.anode, R2.Pin_1
  N30: LED2.anode, R1.Pin_1

custom parts:
  LCM1602 IIC: I2C-Module to use a 1602 or 2004 LCD on with the wire.h libory Serial LCD Modul
  DHT11 Humitidy and Temperature Sensor: DHT11 Humidity and Temperature Sensor
  RFID-RC522-v3: A simple China made RFID-RC522 Reader (6x4 cm); do check the pin labels, as this is a MFRC522 based clone.
